// Logisim project realaluu.circ as structural Verilog: 10 circuits, main circuit Halfadder
module Halfadder (
  input  A,
  input  B,
  output S,
  output C
);

  xor xor_1 (S, A, B);
  and and_1 (C, A, B);
endmodule

module \and  (
  input  [7:0] a,
  input  [7:0] b,
  output [7:0] out_3
);

  assign out_3 = a & b;  // AND_Gate and_1, 8 bits wide
endmodule

module \or  (
  input  [7:0] a,
  input  [7:0] b,
  output [7:0] out_3
);

  assign out_3 = a | b;  // OR_Gate or_1, 8 bits wide
endmodule

module notb (
  input  [7:0] b,
  output [7:0] out_2
);

  assign out_2 = ~b;  // NOT_Gate not_1, 8 bits wide
endmodule

module LSL (
  input  [7:0] B,
  output [7:0] out_2,
  output Ov
);


  assign out_2 = {B[6:0], 1'b0};
  assign Ov = B[7];
endmodule

module LSR (
  input  [7:0] in_1,
  output [7:0] out_2,
  output out_3
);


  assign out_2 = {1'b0, in_1[7:1]};
  assign out_3 = in_1[0];
endmodule

module Fulladder (
  input  c0,
  input  A,
  input  B,
  output S,
  output c1
);

  wire and_1_out, and_2_out, and_3_out, xor_1_out;

  xor xor_1 (xor_1_out, A, B);
  and and_1 (and_1_out, c0, A);
  and and_2 (and_2_out, A, B);
  and and_3 (and_3_out, c0, B);
  xor xor_2 (S, xor_1_out, c0);
  or or_1 (c1, and_1_out, and_2_out, and_3_out);
endmodule

module Somm4 (
  input  a0,
  input  b0,
  input  c0,
  input  a1,
  input  b1,
  input  a2,
  input  b2,
  input  a3,
  input  b3,
  output out_10,
  output out_11,
  output out_12,
  output out_13,
  output out_14
);

  wire fulladder_1_c1, fulladder_2_c1, fulladder_3_c1;

  Fulladder fulladder_1 (.c0(c0), .A(a0), .B(b0), .S(out_10), .c1(fulladder_1_c1));
  Fulladder fulladder_2 (.c0(fulladder_1_c1), .A(a1), .B(b1), .S(out_11), .c1(fulladder_2_c1));
  Fulladder fulladder_3 (.c0(fulladder_2_c1), .A(a2), .B(b2), .S(out_12), .c1(fulladder_3_c1));
  Fulladder fulladder_4 (.c0(fulladder_3_c1), .A(a3), .B(b3), .S(out_13), .c1(out_14));
endmodule

module Flag_z (
  input  [7:0] in_1,
  output out_2
);

  nor nor_1 (out_2, in_1[0], in_1[1], in_1[2], in_1[3], in_1[4], in_1[5], in_1[6], in_1[7]);
endmodule

module sommatore_8bits (
  input  in_1,
  input  in_2,
  input  in_3,
  input  in_4,
  input  in_5,
  input  in_6,
  input  in_7,
  input  in_8,
  input  in_9,
  input  in_10,
  input  in_11,
  input  in_12,
  input  in_13,
  input  in_14,
  input  in_15,
  input  in_16,
  input  in_17,
  output out_18,
  output out_19,
  output out_20,
  output out_21,
  output out_22,
  output out_23,
  output out_24,
  output out_25,
  output out_26
);

  wire somm4_2_out_14;

  Somm4 somm4_1 (
    .a0(in_8), .b0(in_7), .c0(somm4_2_out_14), .a1(in_6), .b1(in_5), .a2(in_4), .b2(in_3), .a3(in_2),
    .b3(in_1), .out_10(out_22), .out_11(out_21), .out_12(out_20), .out_13(out_19), .out_14(out_18));
  Somm4 somm4_2 (
    .a0(in_16), .b0(in_15), .c0(in_17), .a1(in_14), .b1(in_13), .a2(in_12), .b2(in_11), .a3(in_10),
    .b3(in_9), .out_10(out_26), .out_11(out_25), .out_12(out_24), .out_13(out_23), .out_14(somm4_2_out_14));
endmodule
